# Fritzing sketch Puppe5 (saved by Fritzing 0.9.9b)
circuit board: 8cm x 5.3cm
breadboards: 1

parts:
  On/Off = Toggle Switch [package=THT]
  RY2 = srd-05vdc-sl-c
  RY3 = srd-05vdc-sl-c
  RY4 = srd-05vdc-sl-c
  RY5 = srd-05vdc-sl-c
  Q1 = NPN-Transistor [package="TO92 [THT]"]
  Q2 = NPN-Transistor [package="TO92 [THT]"]
  Q3 = NPN-Transistor [package="TO92 [THT]"]
  Q4 = NPN-Transistor [package="TO92 [THT]"]
  J5 = Camdenboss CTB0158-4 [part_number=CTB0158-4 package=THT]
  TP4056 = TP4056 Module [part_number=HW-107]
  Batt = Header 2 [package=jst-2-pth]
  R1 = Resistor [tolerance=±5% resistance=10k power=0.25 package=THT]
  R3 = Resistor [tolerance=±5% resistance=1k power=0.25 package=THT]
  R2 = Resistor [tolerance=±5% resistance=1k power=0.25 package=THT]
  R8 = Resistor [tolerance=±5% resistance=1k power=0.25 package=THT]
  R9 = Resistor [tolerance=±5% resistance=1k power=0.25 package=THT]
  R10 = Resistor [tolerance=±5% resistance=10k power=0.25 package=THT]
  R11 = Resistor [tolerance=±5% resistance=10k power=0.25 package=THT]
  R12 = Resistor [tolerance=±5% resistance=10k power=0.25 package=THT]
  U1V10F5 = female pin header, 3 pins [form="♀ (female)"]
  Servo = Basic Servo
  IO1 = female pin header, 3 pins [form="♀ (female)"]
  R13 = Resistor [tolerance=±5% resistance=100k power=0.25 package=THT]
  27k = Resistor [tolerance=±5% resistance=22k power=0.25 package=THT]
  J6 = Camdenboss CTB0158-4 [part_number=CTB0158-4 package=THT]
  SPI = female pin header, 4 pins [form="♀ (female)"]
  5V- = female pin header, 2 pins [form="♀ (female)"]
  3V- = female pin header, 2 pins [form="♀ (female)"]
  IO2 = female pin header, 3 pins [form="♀ (female)"]
  D1 = Schottky Diode [part_number=1N5817 package="300 mil [THT]"]
  D2 = Schottky Diode [part_number=1N5817 package="300 mil [THT]"]
  D3 = Schottky Diode [part_number=1N5817 package="300 mil [THT]"]
  D4 = Schottky Diode [part_number=1N5817 package="300 mil [THT]"]
  ObenAussen = female pin header, 10 pins [form="♀ (female)"]
  ObenInnen = female pin header, 10 pins [form="♀ (female)"]
  UntenInnen = female pin header, 10 pins [form="♀ (female)"]
  UntenAussen = female pin header, 10 pins [form="♀ (female)"]
  C1 = Capacitor Polarized [package=cpol-radial-100uf-25v]
  U6 = MCP1702 Voltage Regulator [package="TO92 [THT]"]
  C4 = Capacitor [package=cap-pth-small2]
  SDA/SCL = female pin header, 2 pins [form="♀ (female)"]
  MH-ET_Live_Minikit_for_ESP1 = MH-ET Live Minikit for ESP32  # not connected

nets:
  N1: On/Off.COM, TP4056.OUT-#4
  N2: On/Off.L2, U1V10F5.pin1, 27k.Pin_1, U6.Vin
  N3: RY2.pin_1, Q1.C, D2.anode
  N4: RY2.pin_2, J5.pin2
  N5: RY2.pin_4, RY2.pin_5, RY3.pin_4, RY3.pin_5, RY4.pin_4, RY4.pin_5, RY5.pin_4, RY5.pin_5, U1V10F5.pin3, Servo.vcc, IO1.pin2, 5V-.pin1, IO2.pin2, D1.cathode, D2.cathode, D3.cathode, D4.cathode, UntenInnen.pin8
  N6: RY3.pin_1, Q2.C, D3.anode
  N7: RY3.pin_2, J6.pin4
  N8: RY4.pin_1, Q3.C, D4.anode
  N9: RY4.pin_2, J6.pin2
  N10: RY5.pin_1, Q4.C, D1.anode
  N11: RY5.pin_2, J5.pin4
  GND: Q1.E, Q2.E, Q3.E, Q4.E, J5.pin1, J5.pin3, TP4056.OUT-#1, R1.Pin_1, R10.Pin_1, R11.Pin_1, R12.Pin_1, U1V10F5.pin2, Servo.gnd, IO1.pin1, R13.Pin_1, J6.pin1, J6.pin3, 5V-.pin2, 3V-.pin2, IO2.pin1, UntenAussen.pin1, C1.-, U6.GND, C4.1
  N12: Q1.B, R8.Pin_1, R10.Pin_0
  N13: Q2.B, R3.Pin_1, R12.Pin_0
  N14: Q3.B, R2.Pin_1, R11.Pin_0
  N15: Q4.B, R1.Pin_0, R9.Pin_1
  N16: TP4056.BAT-, Batt.1
  N17: TP4056.BAT+, Batt.2
  N18: R3.Pin_0, UntenAussen.pin6
  N19: R2.Pin_0, UntenInnen.pin5
  N20: R8.Pin_0, UntenAussen.pin2
  N21: R9.Pin_0, UntenAussen.pin4
  N22: Servo.pulse, ObenAussen.pin5
  N23: IO1.pin3, UntenInnen.pin2
  N24: R13.Pin_0, 27k.Pin_0, ObenInnen.pin2
  N25: SPI.pin1, ObenInnen.pin7
  N26: SPI.pin2, ObenInnen.pin6
  N27: SPI.pin3, ObenInnen.pin5
  N28: SPI.pin4, ObenInnen.pin4
  N29: 3V-.pin1, C1.+, U6.Vout, C4.2
  N30: IO2.pin3, UntenInnen.pin1
  N31: UntenInnen.pin3, SDA/SCL.pin1
  N32: UntenInnen.pin4, SDA/SCL.pin2

notes:
  Cardio
  © 2022 Christian Baumgartner
  Dummy v1.6
  Resuscitation
  Pulmonary

custom parts:
  TP4056 Module: TP4056 Lithium Battery Charge Management Module Links: TP4056 website
  MCP1702 Voltage Regulator: A MCP1702 Low Dropout Fixed Voltage Regulator (available in 1.2V, 1.5V, 1.8V, 2.5V, 2.8V, 3.0V, 3.3V, 4.0V, 5.0V)
  MH-ET Live Minikit for ESP32: MH-ET Live Minikit for ESP32 ( http://mh.nodebb.com/topic/8/mh-et-live-minikit-for-esp32/2/) PCB footprint is invalid.
